# Fritzing sketch Dos arduinos una pantalla (saved by Fritzing 0.9.3b)
circuit board: 13.6949cm x 6.4163cm
breadboards: 1

parts:
  Componente1 = Arduino Nano (Rev3.0)
  Componente2 = Arduino Nano (Rev3.0)
  CD4048B1 = CD4048B [part_number=CD4048B package="DIP (Dual Inline) [THT]"]
  U1 = LCD-16X2 [package=lcd-16x2]
  R1 = Resistor [tolerance=±5% resistance=220 package=THT]
  R2 = Resistor [tolerance=±5% resistance=220 package=THT]
  R3 = Resistor [tolerance=±5% resistance=220 package=THT]
  R4 = Resistor [tolerance=±5% resistance=220 package=THT]
  R5 = Resistor [tolerance=±5% resistance=220 package=THT]

nets:
  N1: Componente1.GND, Componente2.D2, R3.Pin_1
  N2: Componente1.D2, Componente2.D3, R4.Pin_1
  N3: Componente1.A5, Componente2.A5, CD4048B1.A, R1.Pin_1
  N4: Componente1.A4, Componente2.A4, CD4048B1.EXPAND, R2.Pin_1
  VSS: CD4048B1.J, CD4048B1.Kd, CD4048B1.H, CD4048B1.VSS, U1.VSS, U1.R_W, U1.DB0, U1.DB1, U1.DB3, U1.K, R5.Pin_0
  N5: CD4048B1.G, U1.RS
  N6: CD4048B1.F, U1.E
  N7: CD4048B1.Kc, U1.DB7
  N8: CD4048B1.Ka, U1.DB6
  N9: CD4048B1.D, U1.DB5
  N10: CD4048B1.C, U1.DB4
  N11: CD4048B1.VDD, R1.Pin_0, R2.Pin_0
  N12: U1.VDD, U1.A, R5.Pin_1
  N13: R3.Pin_0, R4.Pin_0
